# Fritzing sketch Circuit_diagram (saved by Fritzing 0.9.3b)
breadboards: 2

parts:
  Part1 = Triple Axis Accelerometer Breakout - ADXL335
  Part2 = Arduino Uno (Rev3) - ICSP
  S1 = Pushbutton [package="[THT]"]
  R1 = Resistor [tolerance=±5% resistance=220 package="2512 [SMD]"]
  Part3 = Arduino Uno (Rev3) - ICSP
  S2 = Pushbutton [package="[THT]"]
  R2 = Resistor [tolerance=±5% resistance=220 package="2512 [SMD]"]
  Part4 = Triple Axis Accelerometer Breakout - ADXL335
  Part5 = HX711 Weighing Sensor Module

nets:
  N1: Part1.ZOUT, Part2.A2
  N2: Part1.YOUT, Part2.A1
  N3: Part1.XOUT, Part2.A0
  GND: Part1.GND, Part2.GND, R1.Pin_0
  VCC: Part1.VCC, Part2.5V, S1.Pin_1, S1.Pin_2
  N4: Part2.D2, S1.Pin_3, S1.Pin_4, R1.Pin_1
  N5: Part3.A0, Part4.XOUT
  N6: Part3.A1, Part4.YOUT
  N7: Part3.A2, Part4.ZOUT
  N8: Part3.D2, S2.Pin_3, S2.Pin_4, R2.Pin_1, Part5.GND
  N9: Part3.D5_PWM, Part5.DO/RX
  N10: Part3.D6_PWM, Part5.CK/TX
  VCC_2: Part3.5V, S2.Pin_1, S2.Pin_2, Part4.VCC, Part5.VCC
  GND_2: Part3.GND, R2.Pin_0, Part4.GND

notes:
  GY-61
  Arduino Uno R3
  Push Button
  Resistor(220 ohm)
  LOAD CELL
  HX711
  Arduino-1 -> Server <- Arduino-2
  ^
  |
  GSM Module
  Arduino-1 Connections :
  Acclerometer -1(Vcc) -> Arduino-1(3.3V)
  Acclerometer -1(Gnd) -> Arduino-1(Gnd)
  Acclerometer -1(X-Pin) -> Arduino-1(A0)
  Acclerometer -1(Y-Pin) -> Arduino-1(A1)
  Acclerometer -1(Z-Pin) -> Arduino-1(A2)
  HX711 (Vcc) -> Arduino-1(5V)
  HX711 (Gnd) -> Arduino-1(Gnd)
  HX711 (DT) -> Arduino-1(2)
  HX711 (SCL) -> Arduino-1(3)
  Button-1(1st End) -> Arduino-1(Resistor-1(680 ohm) , Digital_pin7)
  Button-1(2nd End) -> Arduino-1(5V)
  Resistor-1(2nd end) -> Button-1(1st End)
  Resistor-1(2nd end) -> Arduino-1(Gnd)
  Load Sensor -> HX711 Connections can be found in the Internet.
  Arduino-2 Connections :
  Acclerometer -2(Vcc) -> Arduino-2(3.3V)
  Acclerometer -2(Gnd) -> Arduino-2(Gnd)
  Acclerometer -2(X-Pin) -> Arduino-2(A0)
  Acclerometer -2(Y-Pin) -> Arduino-2(A1)
  Acclerometer -2(Z-Pin) -> Arduino-2(A2)
  Button(1st End) -> Arduino-2(Resistor-2(680 ohm) , Digital_pin7)
  Button-2(2nd End) -> Arduino-2(5V)
  Resistor-2(2nd end) -> Button-2(1st End)
  Resistor-2(2nd end) -> Arduino-2(Gnd)
